# Fritzing sketch wiring_FBV (saved by Fritzing 0.9.0b)
breadboards: 1

parts:
  U5 = RJ45 Jack [part_number=FBV package=rj45-8]
  R2 = Resistor [tolerance=±5% resistance=220 package="0603 [SMD]"]
  R1 = Resistor [tolerance=±5% resistance=220 package="1206 [SMD]"]
  R3 = Resistor [tolerance=±5% resistance=220 package=THT]
  U2 = OPTO_DARL_6N138S [package=8-smd]
  Bauteil2 = Arduino Mega 2560 (Rev3)
  VCC2 = Battery block 9V  # not connected

nets:
  GND: U5.1, U2.C, U2.GND, Bauteil2.GND
  N1: U5.2, Bauteil2.VIN
  N2: U5.6, R2.Pin_1
  N3: U5.7, Bauteil2.D18/TX1
  N4: U5.8, R3.Pin_1
  N5: R2.Pin_0, U2.A
  VCC: R1.Pin_0, R3.Pin_0, U2.VCC, Bauteil2.5V
  N6: R1.Pin_1, Bauteil2.D19/RX1
