# Fritzing sketch wiring_FBV_VOX (saved by Fritzing 0.9.2b)
breadboards: 1

parts:
  FBV = RJ45 Jack [package=rj45-8]
  R2 = Resistor [tolerance=±5% resistance=220 package="0603 [SMD]"]
  R1 = Resistor [tolerance=±5% resistance=220 package="1206 [SMD]"]
  R3 = Resistor [tolerance=±5% resistance=220 package=THT]
  U2 = OPTO_DARL_6N138S [package=8-smd]
  Bauteil2 = Arduino Mega 2560 (Rev3)
  VCC2 = Battery block 9V  # not connected
  R4 = Resistor [tolerance=±5% resistance=220 package=THT]
  U6 = OPTO_DARL_6N138S [package=8-smd]
  R5 = Resistor [tolerance=±5% resistance=220 package="1206 [SMD]"]
  R6 = Resistor [tolerance=±5% resistance=220 package="0603 [SMD]"]
  VOX = RJ45 Jack [package=rj45-8]

nets:
  GND: FBV.1, U2.C, U2.GND, Bauteil2.GND, U6.GND
  N1: FBV.2, Bauteil2.VIN
  N2: FBV.6, R2.Pin_1
  N3: FBV.7, Bauteil2.D18/TX1
  N4: FBV.8, R3.Pin_1
  N5: R2.Pin_0, U2.A
  VCC: R1.Pin_0, R3.Pin_0, U2.VCC, Bauteil2.5V, R4.Pin_0, U6.VCC, R5.Pin_0
  N6: R1.Pin_1, Bauteil2.D19/RX1
  N7: Bauteil2.D17_PWM/RX2, R5.Pin_1
  N8: Bauteil2.D16_PWM/TX2, VOX.7
  N9: R4.Pin_1, VOX.8
  N10: U6.A, R6.Pin_0
  N11: U6.C, VOX.2
