# Fritzing sketch wiring_VOX (saved by Fritzing 0.9.4)
breadboards: 1

parts:
  Bauteil2 = Arduino Mega 2560 (Rev3)
  R4 = Resistor [tolerance=±5% resistance=220 package=THT]
  U6 = OPTO_DARL_6N138S [package=8-smd]
  R5 = Resistor [tolerance=±5% resistance=1k package="1206 [SMD]"]
  R6 = Resistor [tolerance=±5% resistance=220 package="0603 [SMD]"]
  VOX = RJ45 Jack [package=rj45-8]

nets:
  N1: Bauteil2.D17_PWM/RX2, U6.VOUT, R5.Pin_1
  N2: Bauteil2.D16_PWM/TX2, VOX.7
  5V: Bauteil2.5V, R4.Pin_0, U6.VCC, R5.Pin_0
  GND: Bauteil2.GND, U6.GND
  N3: R4.Pin_1, VOX.8
  N4: U6.A, R6.Pin_0
  N5: U6.C, VOX.2
  N6: R6.Pin_1, VOX.1
